# Fritzing sketch HueButton (saved by Fritzing 0.9.2b)
breadboards: 1

parts:
  S5 = Momentary Switch [package=ksa_sealed_tac_switch]
  R1 = Resistor [tolerance=±5% resistance=1k package="1206 [SMD]"]
  Raspberry_Pi1 = Raspberry Pi 2

nets:
  N1: S5.1, R1.Pin_1, Raspberry_Pi1.GPIO18
  N2: S5.3, Raspberry_Pi1.GND
  N3: R1.Pin_0, Raspberry_Pi1.3v3
